// Logisim project OpenCPU.circ as structural Verilog: 4 circuits, main circuit HalfAdder
module HalfAdder (
  input  in_1,
  input  in_2,
  output out_3,
  output out_4
);

  xor xor_1 (out_3, in_1, in_2);
  and and_1 (out_4, in_1, in_2);
endmodule

module FullAdder (
  input  cin,
  input  A,
  input  B,
  output out_4,
  output out_5
);

  wire halfadder_1_out_3, halfadder_1_out_4, halfadder_2_out_4;

  HalfAdder halfadder_1 (.in_1(A), .in_2(B), .out_3(halfadder_1_out_3), .out_4(halfadder_1_out_4));
  HalfAdder halfadder_2 (.in_1(cin), .in_2(halfadder_1_out_3), .out_3(out_4), .out_4(halfadder_2_out_4));
  or or_1 (out_5, halfadder_2_out_4, halfadder_1_out_4);
endmodule

module ALU (
  input  in_1,
  input  in_2,
  input  in_3,
  input  in_4,
  input  in_5,
  input  in_6,
  input  in_7,
  input  in_8,
  input  in_9,
  input  in_10,
  input  in_11,
  input  in_12,
  input  in_13,
  input  in_14,
  input  in_15,
  input  in_16,
  output out_17,
  output out_18,
  output out_19,
  output out_20
);

  wire fulladder_1_out_4, fulladder_1_out_5, fulladder_2_out_4, fulladder_2_out_5, fulladder_3_out_4,
       fulladder_3_out_5, fulladder_4_out_4, fulladder_4_out_5;

  FullAdder fulladder_1 (.cin(in_1), .A(in_2), .B(in_3), .out_4(fulladder_1_out_4), .out_5(fulladder_1_out_5));
  Multiplexer multiplexer_1 (.in0(fulladder_1_out_4), .in1(fulladder_1_out_5), .out(out_17), .sel(in_4));
  FullAdder fulladder_2 (.cin(in_5), .A(in_6), .B(in_7), .out_4(fulladder_2_out_4), .out_5(fulladder_2_out_5));
  Multiplexer multiplexer_2 (.in0(fulladder_2_out_4), .in1(fulladder_2_out_5), .out(out_18), .sel(in_8));
  FullAdder fulladder_3 (.cin(in_9), .A(in_10), .B(in_11), .out_4(fulladder_3_out_4), .out_5(fulladder_3_out_5));
  Multiplexer multiplexer_3 (.in0(fulladder_3_out_4), .in1(fulladder_3_out_5), .out(out_19), .sel(in_12));
  FullAdder fulladder_4 (.cin(in_13), .A(in_14), .B(in_15), .out_4(fulladder_4_out_4), .out_5(fulladder_4_out_5));
  Multiplexer multiplexer_4 (.in0(fulladder_4_out_4), .in1(fulladder_4_out_5), .out(out_20), .sel(in_16));
endmodule

module CPU (
  input  in_1,
  input  in_2,
  input  in_3,
  input  in_4,
  input  in_5,
  input  in_6,
  input  in_7,
  input  in_8,
  input  in_9,
  input  in_10,
  input  in_11,
  input  in_12,
  input  in_13,
  input  in_14,
  input  in_15,
  input  in_16
);

  wire clock_1_out;
  wire [3:0] alu_1_out_17;

  ALU alu_1 (
    .in_1(in_1), .in_2(in_2), .in_3(in_3), .in_4(in_4), .in_5(in_5), .in_6(in_6), .in_7(in_7), .in_8(in_8),
    .in_9(in_9), .in_10(in_10), .in_11(in_11), .in_12(in_12), .in_13(in_13), .in_14(in_14), .in_15(in_15),
    .in_16(in_16), .out_17(alu_1_out_17[0]), .out_18(alu_1_out_17[1]), .out_19(alu_1_out_17[2]),
    .out_20(alu_1_out_17[3]));
  Register #(.width(4)) register_1 (.D(alu_1_out_17), .en(clock_1_out), .clk(clock_1_out));  // open: Q, clr
  Clock clock_1 (.out(clock_1_out));
endmodule
